# Fritzing sketch ESP8266_Sensors (saved by Fritzing 0.9.3b)

parts:
  Part1 = Adafruit Si7021 Temp Humidity [part_number="Adafruit #3251"]
  Part2 = Adafruit TCS34725 RGB Color Sensor [part_number="Adafruit #1334"]
  Sensore_PIR_HC-SR502 = HC-SR501 Body Sensor Module
  U1 = NodeMCU V1.0

nets:
  N1: Part1.SDA, Part2.SDA
  N2: Part1.SCL, Part2.SCL
  GND: Part1.GND, Part2.GND, Sensore_PIR_HC-SR502.GND, U1.GND
  VIN: Part1.VIN, Part2.VIN, U1.Vin
  VCC: Sensore_PIR_HC-SR502.VCC, U1.3V3
  N3: Sensore_PIR_HC-SR502.OUT, U1.D5

custom parts:
  Adafruit Si7021 Temp Humidity: It's summer and you're sweating and your hair's all frizzy and all you really want to know is why the weatherman said this morning that today's relative humidity would max out at a perfectly reasonable 42% when it feels more like 77%. Enter the Si7021 Temperature + Humidity Sensor - the best way to prove the weatherman wrong! This lovely sensor for Silicon labs has ± 3% relative humidity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
  Adafruit TCS34725 RGB Color Sensor: Your electronics can now see in dazzling color with this lovely color light sensor. We found the best color sensor on the market, the TCS34725, which has RGB and Clear light sensing elements. An IR blocking filter, integrated on-chip and localized to the color sensing photodiodes, minimizes the IR spectral component of the incoming light and allows color measurements to be made accurately. The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
  HC-SR501 Body Sensor Module: Pyroelectric Infrared PIR Motion Sensor Detector Module
  NodeMCU V1.0: ESP8266 based NodeMCU
